# Fritzing sketch Thermotrack Digram Attempt2 (saved by Fritzing 1.0.4)
circuit board: 8.46667cm x 5.64444cm
breadboards: 1

parts:
  Mod1 = Raspberry Pi 4B
  J1 = Piezo Speaker
  Part1 = HC-SR501
  R2 = 10k Resistor [package="2512 [SMD]"]  # not connected
  F1 = Fan - Ventilador [package=THT]
  S1 = Momentary Switch [package=ksa_sealed_tac_switch]
  RHT1 = Humidity and Temperature Sensor RHT03
  R3 = PHOTOCELL [package=photocell-kit]
  R4 = 10k Resistor [package="2512 [SMD]"]  # not connected

nets (from the breadboard view):
  N1: Mod1.GPIO2, J1.pin1, S1.3
  GND: Mod1.GND, F1.GND
  N2: Mod1.GPIO4, Part1.GND
  N3: Mod1.GPIO18, Part1.VCC
  N4: Mod1.GPIO27, S1.2
  N5: S1.1, R3.P$1
  N6: RHT1.Vcc, RHT1.GND_2

notes:
  couldnt find an LED on fritzing so we used a photcell instead

custom parts:
  HC-SR501: Pyroelectric Infrared PIR Motion Sensor Detector Module
  10k Resistor: Resistor Basic schematic elements and footprints for 0603, 1206, and PTH resistors.
  Fan - Ventilador: Ventilador de 2 pines, se encuentra comunmente en computadoras de escritorio
